// Logisim project MIPS.circ as structural Verilog: 1 circuit, main circuit main
module main (
  input  CLR,
  input  EN
);

  wire alu_1_p4, alu_1_p5, and_1_out, button_1_out, CLK, controlunit_1_out_3, controlunit_1_out_4,
       controlunit_1_out_5, controlunit_1_out_6, controlunit_1_out_7, controlunit_1_out_8,
       controlunit_1_out_9, controlunit_1_out_10, not_1_out, reg_stage2_1_p18, reg_stage2_1_p19,
       reg_stage2_1_p20, reg_stage2_1_p21, reg_stage2_1_p22, reg_stage2_1_p23, reg_stage2_1_p24,
       reg_stage2_1_p25, reg_stage2_1_p26, reg_stage3_1_p13, reg_stage3_1_p14, reg_stage3_1_p15,
       reg_stage3_1_p16, reg_stage3_1_p17, reg_stage3_1_p18, reg_stage4_1_memtoregw, reg_stage4_1_regwritew;
  wire [3:0] controlunit_1_out_11;
  wire [4:0] multiplexer_3_out, reg_stage2_1_p28, reg_stage2_1_p29, reg_stage3_1_p21, reg_stage4_1_writeregw;
  wire [27:0] bit_extender_2_out, shifter_1_out;
  wire [31:0] adder_1_out, adder_2_out, bit_extender_1_out, datamem_1_rd, instmem_1_out_2, multiplexer_1_out,
       multiplexer_2_out, multiplexer_4_out, multiplexer_5_out, PC_q, reg_stage1_1_instrd,
       reg_stage1_1_pcplus4d, reg_stage2_1_p27, reg_stage2_1_p30, reg_stage2_1_p31, reg_stage3_1_p19,
       reg_stage3_1_p20, reg_stage3_1_p22, reg_stage4_1_aluoutw, reg_stage4_1_readdataw, regfile32_1_rd1,
       regfile32_1_rd2, shifter_2_out;

  Clock clock_1 (.out(CLK));
  // Probe on adder_1_out
  Multiplexer #(.width(32)) multiplexer_1 (
    .in0(adder_1_out), .in1(reg_stage3_1_p22), .out(multiplexer_1_out), .sel(and_1_out));  // open: en
  // Probe on reg_stage3_1_p22
  Multiplexer #(.width(32)) multiplexer_2 (
    .in0(multiplexer_1_out), .in1({adder_1_out[31:28], shifter_1_out}), .out(multiplexer_2_out),
    .sel(controlunit_1_out_4));  // open: en
  Button button_1 (.out(button_1_out));
  Register #(.width(32)) PC (.D(multiplexer_2_out), .Q(PC_q), .clk(CLK), .clr(button_1_out));  // open: en
  InstMem instmem_1 (.A(PC_q), .out_2(instmem_1_out_2));
  Adder #(.width(32)) adder_1 (.a(PC_q), .b(32'h4), .out(adder_1_out));  // open: cin, cout
  Reg_Stage1 reg_stage1_1 (
    .CLR(CLR), .EN(CLR), .CLK(CLK), .InstrF(instmem_1_out_2), .PCPlus4F(adder_1_out),
    .InstrD(reg_stage1_1_instrd), .PCPlus4D(reg_stage1_1_pcplus4d));
  ControlUnit controlunit_1 (
    .out_4(controlunit_1_out_4), .in_1(reg_stage1_1_instrd[31:26]), .in_2(reg_stage1_1_instrd[5:0]),
    .out_5(controlunit_1_out_5), .out_6(controlunit_1_out_6), .out_7(controlunit_1_out_7),
    .out_8(controlunit_1_out_8), .out_9(controlunit_1_out_9), .out_10(controlunit_1_out_10),
    .out_11(controlunit_1_out_11), .out_3(controlunit_1_out_3));
  RegFile32 regfile32_1 (
    .AD1(reg_stage1_1_instrd[25:21]), .AD2(reg_stage1_1_instrd[20:16]), .CLK(CLK),
    .WE(reg_stage4_1_regwritew), .AD3(reg_stage4_1_writeregw), .WD3(multiplexer_5_out),
    .RD1(regfile32_1_rd1), .RD2(regfile32_1_rd2));
  assign bit_extender_1_out = {{16{reg_stage1_1_instrd[15]}}, reg_stage1_1_instrd[15:0]};  // Bit_Extender bit_extender_1
  assign bit_extender_2_out = {{2{reg_stage1_1_instrd[25]}}, reg_stage1_1_instrd[25:0]};  // Bit_Extender bit_extender_2
  Shifter #(.width(28)) shifter_1 (.in(bit_extender_2_out), .\dist (5'b00010), .out(shifter_1_out));
  // Reg_Stage2 reg_stage2_1: pin names not known; wires that end beside it: controlunit_1_out_3, controlunit_1_out_5, controlunit_1_out_6, controlunit_1_out_7, controlunit_1_out_8, controlunit_1_out_9, controlunit_1_out_10, controlunit_1_out_11, regfile32_1_rd1, regfile32_1_rd2, reg_stage1_1_instrd[20:16], reg_stage1_1_instrd[15:11], bit_extender_1_out, reg_stage1_1_pcplus4d, CLR, CLK, CLR, reg_stage2_1_p18, reg_stage2_1_p19, reg_stage2_1_p20, reg_stage2_1_p21, reg_stage2_1_p22, reg_stage2_1_p23, reg_stage2_1_p24, reg_stage2_1_p25, reg_stage2_1_p26, reg_stage2_1_p27, reg_stage2_1_p28, reg_stage2_1_p29, reg_stage2_1_p30, reg_stage2_1_p31
  Multiplexer #(.width(5)) multiplexer_3 (
    .in0(reg_stage2_1_p28), .in1(reg_stage2_1_p29), .out(multiplexer_3_out), .sel(reg_stage2_1_p23));  // open: en
  Multiplexer #(.width(32)) multiplexer_4 (
    .in0(reg_stage2_1_p27), .in1(reg_stage2_1_p30), .out(multiplexer_4_out), .sel(reg_stage2_1_p22));  // open: en
  // Probe on reg_stage2_1_p30
  // ALU alu_1: pin names not known; wires that end beside it: reg_stage2_1_p26, multiplexer_4_out, reg_stage2_1_p25, alu_1_p4, alu_1_p5
  Shifter #(.width(32)) shifter_2 (.in(reg_stage2_1_p30), .\dist (5'b00010), .out(shifter_2_out));
  Adder #(.width(32)) adder_2 (.a(shifter_2_out), .b(reg_stage2_1_p31), .out(adder_2_out));  // open: cin, cout
  not not_1 (not_1_out, reg_stage3_1_p13);
  // Reg_Stage3 reg_stage3_1: pin names not known; wires that end beside it: reg_stage2_1_p18, reg_stage2_1_p19, reg_stage2_1_p20, reg_stage2_1_p21, reg_stage2_1_p24, alu_1_p4, alu_1_p5, reg_stage2_1_p27, multiplexer_3_out, adder_2_out, CLK, CLR, reg_stage3_1_p13, reg_stage3_1_p14, reg_stage3_1_p15, reg_stage3_1_p16, reg_stage3_1_p17, reg_stage3_1_p18, reg_stage3_1_p19, reg_stage3_1_p20, reg_stage3_1_p21, reg_stage3_1_p22
  and and_1 (and_1_out, not_1_out, reg_stage3_1_p16, reg_stage3_1_p18);
  DataMem datamem_1 (.CLK(CLK), .WE(reg_stage3_1_p15), .WD(reg_stage3_1_p20), .A(reg_stage3_1_p19), .RD(datamem_1_rd));
  Reg_Stage4 reg_stage4_1 (
    .CLR(CLR), .EN(CLR), .CLK(CLK), .RegWriteM(reg_stage3_1_p17), .MemtoRegM(reg_stage3_1_p14),
    .ALUOutM(reg_stage3_1_p19), .ReadDataM(datamem_1_rd), .WriteRegM(reg_stage3_1_p21),
    .RegWriteW(reg_stage4_1_regwritew), .MemtoRegW(reg_stage4_1_memtoregw), .ALUOutW(reg_stage4_1_aluoutw),
    .ReadDataW(reg_stage4_1_readdataw), .WriteRegW(reg_stage4_1_writeregw));
  Multiplexer #(.width(32)) multiplexer_5 (
    .in0(reg_stage4_1_aluoutw), .in1(reg_stage4_1_readdataw), .out(multiplexer_5_out),
    .sel(reg_stage4_1_memtoregw));  // open: en

  assign EN = CLR;
endmodule
